// Logisim project DDCA project.circ as structural Verilog: 1 circuit, main circuit main
module main (
  input  in_1,
  input  in_2,
  input  in_3,
  output out_4
);

  wire XOR_out;

  xor XOR (XOR_out, in_1, in_2);
  xor XOR_2 (out_4, XOR_out, in_3);
endmodule
